# Fritzing sketch Coche Fantastico (saved by Fritzing 0.8.5b)
breadboards: 1

parts:
  Parte1 = Arduino Uno (Rev3)
  S1 = Pushbutton [package="[THT]"]
  R1 = Resistor [tolerance=±5% resistance=10k package=THT]
  R2 = Resistor [tolerance=±5% resistance=220 package=THT]
  R3 = Resistor [tolerance=±5% resistance=220 package=THT]
  R4 = Resistor [tolerance=±5% resistance=220 package=THT]
  R5 = Resistor [tolerance=±5% resistance=220 package=THT]
  R6 = Resistor [tolerance=±5% resistance=220 package=THT]
  R7 = Resistor [tolerance=±5% resistance=220 package=THT]
  LED1 = LED - 5mm [color="Red (633nm)" package="5 mm [THT]"]
  LED2 = LED - 5mm [color="Red (633nm)" package="5 mm [THT]"]
  LED3 = LED - 5mm [color="Red (633nm)" package="5 mm [THT]"]
  LED4 = LED - 5mm [color="Red (633nm)" package="5 mm [THT]"]
  LED5 = LED - 5mm [color="Red (633nm)" package="5 mm [THT]"]
  LED6 = LED - 5mm [color="Red (633nm)" package="5 mm [THT]"]

nets:
  N1: Parte1.D8, LED1.anode
  N2: Parte1.D2, S1.Pin_1, S1.Pin_2, R1.Pin_0
  N3: Parte1.D3_PWM, LED6.anode
  N4: Parte1.D4, LED5.anode
  N5: Parte1.D5_PWM, LED4.anode
  N6: Parte1.D6_PWM, LED3.anode
  N7: Parte1.D7, LED2.anode
  N8: Parte1.3V3, R1.Pin_1, R2.Pin_1, R3.Pin_1, R4.Pin_1, R5.Pin_1, R6.Pin_1, R7.Pin_1
  N9: Parte1.5V, S1.Pin_3, S1.Pin_4
  N10: R2.Pin_0, LED1.cathode
  N11: R3.Pin_0, LED2.cathode
  N12: R4.Pin_0, LED3.cathode
  N13: R5.Pin_0, LED4.cathode
  N14: R6.Pin_0, LED5.cathode
  N15: R7.Pin_0, LED6.cathode
