# Fritzing sketch LCD_Serial_16x2 (saved by Fritzing 0.9.3b)
breadboards: 1

parts:
  Parte1 = Arduino Uno (Rev3)
  LCD1 = LCD screen
  R1 = Trimmer Potentiometer [maximum_resistance=10kΩ package=THT]

nets:
  N1: Parte1.D8, LCD1.DB4
  N2: Parte1.D9_PWM, LCD1.DB5
  N3: Parte1.D10_PWM/SS, LCD1.DB6
  N4: Parte1.D11_PWM/MOSI, LCD1.DB7
  N5: Parte1.D6_PWM, LCD1.RS
  N6: Parte1.D7, LCD1.E
  5V: Parte1.5V, LCD1.VDD, LCD1.LED+, R1.leg2
  GND: Parte1.GND, LCD1.VSS, LCD1.R/W, LCD1.LED-, R1.leg1
  N7: LCD1.V0, R1.wiper
