# Fritzing sketch LedsConPotenciometro (saved by Fritzing 0.8.5b)
breadboards: 1

parts:
  LED1 = LED - 5mm [color="Green (555nm)" package="5 mm [THT]"]
  LED4 = LED - 5mm [color="Yellow (585nm)" package="5 mm [THT]"]
  LED8 = LED - 5mm [color="Red (633nm)" package="5 mm [THT]"]
  LED9 = LED - 5mm [color="Red (633nm)" package="5 mm [THT]"]
  LED10 = LED - 5mm [color="Red (633nm)" package="5 mm [THT]"]
  R1 = Resistor [tolerance=±5% resistance=220 package=THT]
  R2 = Resistor [tolerance=±5% resistance=220 package=THT]
  R3 = Resistor [tolerance=±5% resistance=220 package=THT]
  R4 = Resistor [tolerance=±5% resistance=220 package=THT]
  R5 = Resistor [tolerance=±5% resistance=220 package=THT]
  R6 = Resistor [tolerance=±5% resistance=220 package=THT]
  R7 = Resistor [tolerance=±5% resistance=220 package=THT]
  R8 = Resistor [tolerance=±5% resistance=220 package=THT]
  R9 = Resistor [tolerance=±5% resistance=220 package=THT]
  R10 = Resistor [tolerance=±5% resistance=220 package=THT]
  LED11 = LED - 5mm [color="Green (555nm)" package="5 mm [THT]"]
  LED12 = LED - 5mm [color="Green (555nm)" package="5 mm [THT]"]
  LED13 = LED - 5mm [color="Yellow (585nm)" package="5 mm [THT]"]
  LED14 = LED - 5mm [color="Yellow (585nm)" package="5 mm [THT]"]
  LED15 = LED - 5mm [color="Yellow (585nm)" package="5 mm [THT]"]
  R11 = Rotary Potentiometer (Small) [maximum_resistance=100kΩ package=THT]
  Parte1 = Arduino Uno (Rev3)

nets:
  N1: LED1.cathode, Parte1.D0/RX
  N2: LED1.anode, R10.Pin_0
  N3: LED4.cathode, Parte1.D4
  N4: LED4.anode, R7.Pin_0
  N5: LED8.cathode, Parte1.D8
  N6: LED8.anode, R3.Pin_0
  N7: LED9.cathode, Parte1.D9_PWM
  N8: LED9.anode, R2.Pin_0
  N9: LED10.cathode, Parte1.D10_PWM/SS
  N10: LED10.anode, R1.Pin_0
  N11: R1.Pin_1, R2.Pin_1, R3.Pin_1, R4.Pin_1, R5.Pin_1, R6.Pin_1, R7.Pin_1, R8.Pin_1, R9.Pin_1, R10.Pin_1, R11.leg2, Parte1.GND
  N12: R4.Pin_0, LED15.anode
  N13: R5.Pin_0, LED14.anode
  N14: R6.Pin_0, LED13.anode
  N15: R8.Pin_0, LED12.anode
  N16: R9.Pin_0, LED11.anode
  N17: LED11.cathode, Parte1.D1/TX
  N18: LED12.cathode, Parte1.D2
  N19: LED13.cathode, Parte1.D5_PWM
  N20: LED14.cathode, Parte1.D6_PWM
  N21: LED15.cathode, Parte1.D7
  N22: R11.leg1, Parte1.5V
  N23: R11.wiper, Parte1.A0
