# Fritzing sketch Esquema4Led1Pulsador (saved by Fritzing 0.8.5b)
breadboards: 1

parts:
  Parte1 = Arduino Uno (Rev3)
  LED1 = LED - 5mm [color="Blue (430nm)" package="5 mm [THT]"]
  LED2 = LED - 5mm [color="Blue (430nm)" package="5 mm [THT]"]
  LED3 = LED - 5mm [color="Red (633nm)" package="5 mm [THT]"]
  LED4 = LED - 5mm [color="Red (633nm)" package="5 mm [THT]"]
  R1 = Resistor [tolerance=±5% resistance=220 package=THT]
  R2 = Resistor [tolerance=±5% resistance=220 package=THT]
  R3 = Resistor [tolerance=±5% resistance=220 package=THT]
  R4 = Resistor [tolerance=±5% resistance=220 package=THT]
  S1 = Pushbutton [package="[THT]"]
  R5 = Resistor [tolerance=±5% resistance=10 package=THT]

nets:
  N1: Parte1.D10_PWM/SS, LED3.cathode
  N2: Parte1.D11_PWM/MOSI, LED4.cathode
  N3: Parte1.D12/MISO, Parte1.GND, R1.Pin_1, R2.Pin_1, R3.Pin_1, R4.Pin_1, R5.Pin_1
  N4: Parte1.D5_PWM, LED2.cathode
  N5: Parte1.D6_PWM, LED1.cathode
  N6: Parte1.5V, S1.Pin_1, S1.Pin_2, R5.Pin_0
  N7: LED1.anode, R2.Pin_0
  N8: LED2.anode, R1.Pin_0
  N9: LED3.anode, R3.Pin_0
  N10: LED4.anode, R4.Pin_0
  N11: S1.Pin_3, S1.Pin_4
