# Fritzing sketch RFID (saved by Fritzing 0.8.7b)
circuit board: 8.46667cm x 5.64444cm
breadboards: 1

parts:
  Bauteil1 = Arduino Uno (Rev3)
  RC522 = RFID-RC522

nets:
  N1: Bauteil1.D9_PWM, RC522.RST
  N2: Bauteil1.D10_PWM/SS, RC522.SDA
  N3: Bauteil1.D11_PWM/MOSI, RC522.MOSI
  N4: Bauteil1.D12/MISO, RC522.MISO
  N5: Bauteil1.D13/SCK, RC522.SCK
  N6: Bauteil1.3V3, RC522.3_3V
  GND: Bauteil1.GND, RC522.GND

custom parts:
  RFID-RC522: The simple China made RFID reader
